// Logisim project lcd2.circ as structural Verilog: 1 circuit, main circuit main
module main (
  input  [7:0] in_1,
  input  [7:0] in_2,
  input  [7:0] in_3,
  input  [7:0] in_4,
  input  in_5,
  input  Up_Down,
  input  Unsigned_Signed,
  input  Dec_Hex,
  input  in_9,
  input  in_10,
  input  in_11,
  input  in_12,
  output out_13,
  output out_14,
  output out_15,
  output out_16
);

  wire CLK_2_out, CLK_3_out, CLK_out, clock_1_out, clock_2_out, dip_74139_1_p4, dip_74139_1_p5,
       dip_74139_1_p6, dip_74139_1_p7, dip_74139_2_p4, dip_74139_2_p5, dip_74139_2_p6, dip_74139_2_p7,
       dip_74161_1_p7, dip_74161_3_p9, dip_74161_3_p10, dip_74161_3_p11, dip_74161_3_p12, RST_2_out,
       RST_3_out, RST_out;
  wire [7:0] counter_1_q, dip_74161_1_p8, multiplexer_1_out, multiplexer_2_out, multiplexer_3_out,
       multiplexer_4_out, multiplexer_5_out, multiplexer_6_out, multiplexer_7_out, multiplexer_8_out,
       rom_1_data, rom_2_data, rom_3_data;

  Clock clock_1 (.out(clock_1_out));
  // DIP_7476 dip_7476_1: pin names not known; wires that end beside it: clock_1_out, 1'b1, out_14, 1'b1, out_14, 1'b1, out_13, 1'b1
  Button RST (.out(RST_out));
  Button CLK (.out(CLK_out));
  // DIP_74163 dip_74163_1: pin names not known
  // DIP_74139 dip_74139_1: pin names not known; wires that end beside it: 1'b0, out_14, out_13, dip_74139_1_p4, dip_74139_1_p5, dip_74139_1_p6, dip_74139_1_p7
  // NOT_Gate not_1 has open pins: in=RST_out, out=open
  // DIP_74161 dip_74161_1: pin names not known; wires that end beside it: CLK_out, 1'b0, 1'b0, 1'b0, 1'b0, 1'b1, dip_74161_1_p7, dip_74161_1_p8[0], dip_74161_1_p8[1], dip_74161_1_p8[2], dip_74161_1_p8[3], 1'b1
  // NOT_Gate not_2 has open pins: in=RST_out, out=open
  // DIP_74161 dip_74161_2: pin names not known; wires that end beside it: dip_74161_1_p7, 1'b0, 1'b0, 1'b0, 1'b0, 1'b1, 1'b1, dip_74161_1_p8[4], dip_74161_1_p8[5], dip_74161_1_p8[6], dip_74161_1_p8[7], 1'b1, 1'b1
  Counter counter_1 (
    .load(Up_Down), .count(1'b1), .Q(counter_1_q), .clk(CLK_2_out), .clr(RST_2_out));  // open: D, carry
  Button CLK_2 (.out(CLK_2_out));
  Button RST_2 (.out(RST_2_out));
  Clock clock_2 (.out(clock_2_out));
  Button RST_3 (.out(RST_3_out));
  Button CLK_3 (.out(CLK_3_out));
  // Probe on in_4
  // Probe on in_4
  // DIP_7476 dip_7476_2: pin names not known; wires that end beside it: clock_2_out, 1'b1, out_16, 1'b1, out_16, 1'b1, out_15, 1'b1
  // NOT_Gate not_3 has open pins: in=RST_3_out, out=open
  // DIP_74161 dip_74161_3: pin names not known; wires that end beside it: CLK_3_out, in_9, in_9, in_9, in_9, in_10, in_11, in_12, dip_74161_3_p9, dip_74161_3_p10, dip_74161_3_p11, dip_74161_3_p12
  ROM rom_1 (.addr(in_1), .data(rom_1_data), .sel(1'b1));
  // Probe on counter_1_q
  // DIP_74139 dip_74139_2: pin names not known; wires that end beside it: 1'b0, out_16, out_15, dip_74139_2_p4, dip_74139_2_p5, dip_74139_2_p6, dip_74139_2_p7
  // NOT_Gate not_4 has open pins: in=open, out=dip_74161_3_p9
  // NOT_Gate not_5 has open pins: in=open, out=dip_74161_3_p10
  // NOT_Gate not_6 has open pins: in=open, out=dip_74161_3_p11
  // NOT_Gate not_7 has open pins: in=open, out=dip_74161_3_p12
  _7_Segment_Display u_7_segment_display_1 (
    .g(rom_1_data[0]), .f(rom_1_data[1]), .a(rom_1_data[6]), .b(rom_1_data[5]), .e(rom_1_data[2]),
    .d(rom_1_data[3]), .c(rom_1_data[4]), .dp(rom_1_data[7]));
  ROM #(.addrWidth(11)) rom_2 (.addr({in_5, out_13, out_14, in_4}), .data(rom_2_data));  // open: sel
  // Probe on counter_1_q
  Multiplexer #(.width(8), .enable("false")) multiplexer_1 (
    .in0(rom_2_data), .in1({8{1'b0}}), .out(multiplexer_1_out), .sel(dip_74139_1_p7));
  Multiplexer #(.width(8), .enable("false")) multiplexer_2 (
    .in0(rom_2_data), .in1({8{1'b0}}), .out(multiplexer_2_out), .sel(dip_74139_1_p6));
  Multiplexer #(.width(8), .enable("false")) multiplexer_3 (
    .in0(rom_2_data), .in1({8{1'b0}}), .out(multiplexer_3_out), .sel(dip_74139_1_p5));
  Multiplexer #(.width(8), .enable("false")) multiplexer_4 (
    .in0(rom_2_data), .in1({8{1'b0}}), .out(multiplexer_4_out), .sel(dip_74139_1_p4));
  ROM #(.addrWidth(12)) rom_3 (
    .addr({Dec_Hex, Unsigned_Signed, out_15, out_16, counter_1_q}), .data(rom_3_data));  // open: sel
  _7_Segment_Display u_7_segment_display_2 (
    .g(multiplexer_1_out[0]), .f(multiplexer_1_out[1]), .a(multiplexer_1_out[6]), .b(multiplexer_1_out[5]),
    .e(multiplexer_1_out[2]), .d(multiplexer_1_out[3]), .c(multiplexer_1_out[4]), .dp(multiplexer_1_out[7]));
  Multiplexer #(.width(8), .enable("false")) multiplexer_5 (
    .in0(rom_3_data), .in1({8{1'b0}}), .out(multiplexer_5_out), .sel(dip_74139_2_p7));
  Multiplexer #(.width(8), .enable("false")) multiplexer_6 (
    .in0(rom_3_data), .in1({8{1'b0}}), .out(multiplexer_6_out), .sel(dip_74139_2_p6));
  Multiplexer #(.width(8), .enable("false")) multiplexer_7 (
    .in0(rom_3_data), .in1({8{1'b0}}), .out(multiplexer_7_out), .sel(dip_74139_2_p5));
  _7_Segment_Display u_7_segment_display_3 (
    .g(in_3[0]), .f(in_3[1]), .a(in_3[6]), .b(in_3[5]), .e(in_3[2]), .d(in_3[3]), .c(in_3[4]), .dp(in_3[7]));
  _7_Segment_Display u_7_segment_display_4 (
    .g(multiplexer_2_out[0]), .f(multiplexer_2_out[1]), .a(multiplexer_2_out[6]), .b(multiplexer_2_out[5]),
    .e(multiplexer_2_out[2]), .d(multiplexer_2_out[3]), .c(multiplexer_2_out[4]), .dp(multiplexer_2_out[7]));
  _7_Segment_Display u_7_segment_display_5 (
    .g(multiplexer_3_out[0]), .f(multiplexer_3_out[1]), .a(multiplexer_3_out[6]), .b(multiplexer_3_out[5]),
    .e(multiplexer_3_out[2]), .d(multiplexer_3_out[3]), .c(multiplexer_3_out[4]), .dp(multiplexer_3_out[7]));
  Multiplexer #(.width(8), .enable("false")) multiplexer_8 (
    .in0(rom_3_data), .in1({8{1'b0}}), .out(multiplexer_8_out), .sel(dip_74139_2_p4));
  _7_Segment_Display u_7_segment_display_6 (
    .g(multiplexer_4_out[0]), .f(multiplexer_4_out[1]), .a(multiplexer_4_out[6]), .b(multiplexer_4_out[5]),
    .e(multiplexer_4_out[2]), .d(multiplexer_4_out[3]), .c(multiplexer_4_out[4]), .dp(multiplexer_4_out[7]));
  _7_Segment_Display u_7_segment_display_7 (
    .g(multiplexer_5_out[0]), .f(multiplexer_5_out[1]), .a(multiplexer_5_out[6]), .b(multiplexer_5_out[5]),
    .e(multiplexer_5_out[2]), .d(multiplexer_5_out[3]), .c(multiplexer_5_out[4]), .dp(multiplexer_5_out[7]));
  _7_Segment_Display u_7_segment_display_8 (
    .g(multiplexer_6_out[0]), .f(multiplexer_6_out[1]), .a(multiplexer_6_out[6]), .b(multiplexer_6_out[5]),
    .e(multiplexer_6_out[2]), .d(multiplexer_6_out[3]), .c(multiplexer_6_out[4]), .dp(multiplexer_6_out[7]));
  _7_Segment_Display u_7_segment_display_9 (
    .g(multiplexer_7_out[0]), .f(multiplexer_7_out[1]), .a(multiplexer_7_out[6]), .b(multiplexer_7_out[5]),
    .e(multiplexer_7_out[2]), .d(multiplexer_7_out[3]), .c(multiplexer_7_out[4]), .dp(multiplexer_7_out[7]));
  // Probe on in_2
  _7_Segment_Display u_7_segment_display_10 (
    .g(multiplexer_8_out[0]), .f(multiplexer_8_out[1]), .a(multiplexer_8_out[6]), .b(multiplexer_8_out[5]),
    .e(multiplexer_8_out[2]), .d(multiplexer_8_out[3]), .c(multiplexer_8_out[4]), .dp(multiplexer_8_out[7]));
  _7_Segment_Display u_7_segment_display_11 (
    .g(in_2[0]), .f(in_2[1]), .a(in_2[6]), .b(in_2[5]), .e(in_2[2]), .d(in_2[3]), .c(in_2[4]), .dp(in_2[7]));

  // Notes on the sheet:
  //   contents of rom_1 (hex, n*v repeats v):
  //   7e 30 6d 79 33 5b 5f 70 7f 7b
  //   Up 4 Bit
  //   contents of rom_2 (hex, n*v repeats v):
  //   7e 30 6d 79 33 5b 5f 70 7f 7b 7e 30 6d 79 33 5b 5f 70 7f 7b 7e 30 6d 79 33 5b 5f 70 7f 7b 7e 30 6d
  //   79 33 5b 5f 70 7f 7b 7e 30 6d 79 33 5b 5f 70 7f 7b 7e 30 6d 79 33 5b 5f 70 7f 7b 7e 30 6d 79 33 5b
  //   5f 70 7f 7b 7e 30 6d 79 33 5b 5f 70 7f 7b 7e 30 6d 79 33 5b 5f 70 7f 7b 7e 30 6d 79 33 5b 5f 70 7f
  //   7b 7e 30 6d 79 33 5b 5f 70 7f 7b 7e 30 6d 79 33 5b 5f 70 7f 7b 7e 30 6d 79 33 5b 5f 70 7f 7b 7e 30
  //   6d 79 33 5b 5f 70 7f 7b 7e 30 6d 79 33 5b 5f 70 7f 7b 7e 30 6d 79 33 5b 5f 70 7f 7b 7e 30 6d 79 33
  //   5b 5f 70 7f 7b 7e 30 6d 79 33 5b 5f 70 7f 7b 7e 30 6d 79 33 5b 5f 70 7f 7b 7e 30 6d 79 33 5b 5f 70
  //   7f 7b 7e 30 6d 79 33 5b 5f 70 7f 7b 7e 30 6d 79 33 5b 5f 70 7f 7b 7e 30 6d 79 33 5b 5f 70 7f 7b 7e
  //   30 6d 79 33 5b 5f 70 7f 7b 7e 30 6d 79 33 5b 5f 70 7f 7b 7e 30 6d 79 33 5b 10*7e 10*30 10*6d 10*79
  //   10*33 10*5b 10*5f 10*70 10*7f 10*7b 10*7e 10*30 10*6d 10*79 10*33 10*5b 10*5f 10*70 10*7f 10*7b
  //   10*7e 10*30 10*6d 10*79 10*33 6*5b 100*7e 100*30 56*6d 256*0 7e 30 6d 79 33 5b 5f 70 7f 7b 7e 30 6d
  //   79 33 5b 5f 70 7f 7b 7e 30 6d 79 33 5b 5f 70 7f 7b 7e 30 6d 79 33 5b 5f 70 7f 7b 7e 30 6d 79 33 5b
  //   5f 70 7f 7b 7e 30 6d 79 33 5b 5f 70 7f 7b 7e 30 6d 79 33 5b 5f 70 7f 7b 7e 30 6d 79 33 5b 5f 70 7f
  //   7b 7e 30 6d 79 33 5b 5f 70 7f 7b 7e 30 6d 79 33 5b 5f 70 7f 7b 7e 30 6d 79 33 5b 5f 70 7f 7b 7e 30
  //   6d 79 33 5b 5f 70 7f 7b 7e 30 6d 79 33 5b 5f 70 7f 70 5f 5b 33 79 6d 30 7e 7b 7f 70 5f 5b 33 79 6d
  //   30 7e 7b 7f 70 5f 5b 33 79 6d 30 7e 7b 7f 70 5f 5b 33 79 6d 30 7e 7b 7f 70 5f 5b 33 79 6d 30 7e 7b
  //   7f 70 5f 5b 33 79 6d 30 7e 7b 7f 70 5f 5b 33 79 6d 30 7e 7b 7f 70 5f 5b 33 79 6d 30 7e 7b 7f 70 5f
  //   5b 33 79 6d 30 7e 7b 7f 70 5f 5b 33 79 6d 30 7e 7b 7f 70 5f 5b 33 79 6d 30 7e 7b 7f 70 5f 5b 33 79
  //   6d 30 7e 7b 7f 70 5f 5b 33 79 6d 30 10*7e 10*30 10*6d 10*79 10*33 10*5b 10*5f 10*70 10*7f 10*7b
  //   10*7e 10*30 17*6d 10*30 10*7e 10*7b 10*7f 10*70 10*5f 10*5b 10*33 10*79 10*6d 10*30 109*7e 57*30
  //   99*7e 128*0 128*1
  //   Down 4 Bit
  //   contents of rom_3 (hex, n*v repeats v):
  //   7e 30 6d 79 33 5b 5f 70 7f 7b 7e 30 6d 79 33 5b 5f 70 7f 7b 7e 30 6d 79 33 5b 5f 70 7f 7b 7e 30 6d
  //   79 33 5b 5f 70 7f 7b 7e 30 6d 79 33 5b 5f 70 7f 7b 7e 30 6d 79 33 5b 5f 70 7f 7b 7e 30 6d 79 33 5b
  //   5f 70 7f 7b 7e 30 6d 79 33 5b 5f 70 7f 7b 7e 30 6d 79 33 5b 5f 70 7f 7b 7e 30 6d 79 33 5b 5f 70 7f
  //   7b 7e 30 6d 79 33 5b 5f 70 7f 7b 7e 30 6d 79 33 5b 5f 70 7f 7b 7e 30 6d 79 33 5b 5f 70 7f 7b 7e 30
  //   6d 79 33 5b 5f 70 7f 7b 7e 30 6d 79 33 5b 5f 70 7f 7b 7e 30 6d 79 33 5b 5f 70 7f 7b 7e 30 6d 79 33
  //   5b 5f 70 7f 7b 7e 30 6d 79 33 5b 5f 70 7f 7b 7e 30 6d 79 33 5b 5f 70 7f 7b 7e 30 6d 79 33 5b 5f 70
  //   7f 7b 7e 30 6d 79 33 5b 5f 70 7f 7b 7e 30 6d 79 33 5b 5f 70 7f 7b 7e 30 6d 79 33 5b 5f 70 7f 7b 7e
  //   30 6d 79 33 5b 5f 70 7f 7b 7e 30 6d 79 33 5b 5f 70 7f 7b 7e 30 6d 79 33 5b 10*7e 10*30 10*6d 10*79
  //   10*33 10*5b 10*5f 10*70 10*7f 10*7b 10*7e 10*30 10*6d 10*79 10*33 10*5b 10*5f 10*70 10*7f 10*7b
  //   10*7e 10*30 10*6d 10*79 10*33 6*5b 100*7e 100*30 56*6d 256*0 7e 30 6d 79 33 5b 5f 70 7f 7b 7e 30 6d
  //   79 33 5b 5f 70 7f 7b 7e 30 6d 79 33 5b 5f 70 7f 7b 7e 30 6d 79 33 5b 5f 70 7f 7b 7e 30 6d 79 33 5b
  //   5f 70 7f 7b 7e 30 6d 79 33 5b 5f 70 7f 7b 7e 30 6d 79 33 5b 5f 70 7f 7b 7e 30 6d 79 33 5b 5f 70 7f
  //   7b 7e 30 6d 79 33 5b 5f 70 7f 7b 7e 30 6d 79 33 5b 5f 70 7f 7b 7e 30 6d 79 33 5b 5f 70 7f 7b 7e 30
  //   6d 79 33 5b 5f 70 7f 7b 7e 30 6d 79 33 5b 5f 70 7f 70 5f 5b 33 79 6d 30 7e 7b 7f 70 5f 5b 33 79 6d
  //   30 7e 7b 7f 70 5f 5b 33 79 6d 30 7e 7b 7f 70 5f 5b 33 79 6d 30 7e 7b 7f 70 5f 5b 33 79 6d 30 7e 7b
  //   7f 70 5f 5b 33 79 6d 30 7e 7b 7f 70 5f 5b 33 79 6d 30 7e 7b 7f 70 5f 5b 33 79 6d 30 7e 7b 7f 70 5f
  //   5b 33 79 6d 30 7e 7b 7f 70 5f 5b 33 79 6d 30 7e 7b 7f 70 5f 5b 33 79 6d 30 7e 7b 7f 70 5f 5b 33 79
  //   6d 30 7e 7b 7f 70 5f 5b 33 79 6d 30 10*7e 10*30 10*6d 10*79 10*33 10*5b 10*5f 10*70 10*7f 10*7b
  //   10*7e 10*30 17*6d 10*30 10*7e 10*7b 10*7f 10*70 10*5f 10*5b 10*33 10*79 10*6d 10*30 109*7e 57*30
  //   99*7e 128*0 128*1 7e 30 6d 79 33 5b 5f 70 7f 7b 7d 1f 4e 3d 4f 47 7e 30 6d 79 33 5b 5f 70 7f 7b 7d
  //   1f 4e 3d 4f 47 7e 30 6d 79 33 5b 5f 70 7f 7b 7d 1f 4e 3d 4f 47 7e 30 6d 79 33 5b 5f 70 7f 7b 7d 1f
  //   4e 3d 4f 47 7e 30 6d 79 33 5b 5f 70 7f 7b 7d 1f 4e 3d 4f 47 7e 30 6d 79 33 5b 5f 70 7f 7b 7d 1f 4e
  //   3d 4f 47 7e 30 6d 79 33 5b 5f 70 7f 7b 7d 1f 4e 3d 4f 47 7e 30 6d 79 33 5b 5f 70 7f 7b 7d 1f 4e 3d
  //   4f 47 7e 30 6d 79 33 5b 5f 70 7f 7b 7d 1f 4e 3d 4f 47 7e 30 6d 79 33 5b 5f 70 7f 7b 7d 1f 4e 3d 4f
  //   47 7e 30 6d 79 33 5b 5f 70 7f 7b 7d 1f 4e 3d 4f 47 7e 30 6d 79 33 5b 5f 70 7f 7b 7d 1f 4e 3d 4f 47
  //   7e 30 6d 79 33 5b 5f 70 7f 7b 7d 1f 4e 3d 4f 47 7e 30 6d 79 33 5b 5f 70 7f 7b 7d 1f 4e 3d 4f 47 7e
  //   30 6d 79 33 5b 5f 70 7f 7b 7d 1f 4e 3d 4f 47 7e 30 6d 79 33 5b 5f 70 7f 7b 7d 1f 4e 3d 4f 47 16*7e
  //   16*30 16*6d 16*79 16*33 16*5b 16*5f 16*70 16*7f 16*7b 16*7d 16*1f 16*4e 16*3d 16*4f 16*47 256*7e
  //   256*0 7e 30 6d 79 33 5b 5f 70 7f 7b 7d 1f 4e 3d 4f 47 7e 30 6d 79 33 5b 5f 70 7f 7b 7d 1f 4e 3d 4f
  //   47 7e 30 6d 79 33 5b 5f 70 7f 7b 7d 1f 4e 3d 4f 47 7e 30 6d 79 33 5b 5f 70 7f 7b 7d 1f 4e 3d 4f 47
  //   7e 30 6d 79 33 5b 5f 70 7f 7b 7d 1f 4e 3d 4f 47 7e 30 6d 79 33 5b 5f 70 7f 7b 7d 1f 4e 3d 4f 47 7e
  //   30 6d 79 33 5b 5f 70 7f 7b 7d 1f 4e 3d 4f 47 7e 30 6d 79 33 5b 5f 70 7f 7b 7d 1f 4e 3d 4f 47 7e 47
  //   4f 3d 4e 1f 7d 7b 7f 70 5f 5b 33 79 6d 30 7e 47 4f 3d 4e 1f 7d 7b 7f 70 5f 5b 33 79 6d 30 7e 47 4f
  //   3d 4e 1f 7d 7b 7f 70 5f 5b 33 79 6d 30 7e 47 4f 3d 4e 1f 7d 7b 7f 70 5f 5b 33 79 6d 30 7e 47 4f 3d
  //   4e 1f 7d 7b 7f 70 5f 5b 33 79 6d 30 7e 47 4f 3d 4e 1f 7d 7b 7f 70 5f 5b 33 79 6d 30 7e 47 4f 3d 4e
  //   1f 7d 7b 7f 70 5f 5b 33 79 6d 30 7e 47 4f 3d 4e 1f 7d 7b 7f 70 5f 5b 33 79 6d 30 16*7e 16*30 16*6d
  //   16*79 16*33 16*5b 16*5f 16*70 7f 16*70 16*5f 16*5b 16*33 16*79 16*6d 16*30 271*7e 128*0 128*1
endmodule
